# Fritzing sketch distance-servo (saved by Fritzing 0.9.4)
breadboards: 1

parts:
  Part1 = Arduino Uno (Rev3)
  HC-SR04_Sensor_1 = HC-SR04 Ultrasonic Distance Sensor
  M1 = Dagu DGServo 9g (Pan and tilt) [part_number=RS001B]

nets:
  N1: Part1.D9_PWM, M1.pulse
  N2: Part1.D2, HC-SR04_Sensor_1.TRIG
  N3: Part1.D3_PWM, HC-SR04_Sensor_1.ECHO
  VCC: Part1.5V, HC-SR04_Sensor_1.VCC, M1.vcc
  GND: Part1.GND, HC-SR04_Sensor_1.GND, M1.gnd
